// Logisim project BubbleSort.circ as structural Verilog: 1 circuit, main circuit main
module main (
  input  mux_in,
  input  wr_last,
  input  wr_bigger
);

  wire button_1_out, clock_1_out, comparator_1_lt, comparator_2_eq, not_1_out;
  wire [7:0] counter_1_q;
  wire [31:0] multiplexer_1_out, multiplexer_2_out, ram_1_data, register_1_q, register_2_q, register_3_q,
       register_4_q, register_5_q, register_6_q, register_7_q, register_8_q, register_9_q, register_10_q,
       register_11_q;

  Counter counter_1 (.Q(counter_1_q), .clk(clock_1_out), .clr(button_1_out));  // open: load, D, count, carry
  RAM #(.dataWidth(32)) ram_1 (.addr(counter_1_q), .data(ram_1_data));  // open: sel, clk, ld, clr
  Clock clock_1 (.out(clock_1_out));
  Button button_1 (.out(button_1_out));
  Register #(.width(32)) register_1 (
    .D(multiplexer_1_out), .Q(register_1_q), .clk(clock_1_out), .clr(button_1_out));  // open: en
  Multiplexer #(.width(32)) multiplexer_1 (
    .in0(ram_1_data), .in1(multiplexer_2_out), .out(multiplexer_1_out), .sel(mux_in));  // open: en
  not not_1 (not_1_out, wr_bigger);
  Register #(.width(32)) register_2 (
    .D(register_1_q), .Q(register_2_q), .clk(clock_1_out), .clr(button_1_out));  // open: en
  Register #(.width(32)) register_3 (
    .D(register_2_q), .Q(register_3_q), .clk(clock_1_out), .clr(button_1_out));  // open: en
  Register #(.width(32)) register_4 (
    .D(register_3_q), .Q(register_4_q), .clk(clock_1_out), .clr(button_1_out));  // open: en
  Register #(.width(32)) register_5 (
    .D(register_4_q), .Q(register_5_q), .clk(clock_1_out), .clr(button_1_out));  // open: en
  Register #(.width(32)) register_6 (
    .D(register_5_q), .Q(register_6_q), .clk(clock_1_out), .clr(button_1_out));  // open: en
  Register #(.width(32)) register_7 (
    .D(register_6_q), .Q(register_7_q), .clk(clock_1_out), .clr(button_1_out));  // open: en
  Multiplexer #(.width(32)) multiplexer_2 (
    .in0(register_11_q), .in1(register_9_q), .out(multiplexer_2_out), .sel(not_1_out));  // open: en
  Register #(.width(32)) register_8 (
    .D(register_7_q), .Q(register_8_q), .clk(clock_1_out), .clr(button_1_out));  // open: en
  Register #(.width(32)) register_9 (
    .D(register_8_q), .Q(register_9_q), .clk(clock_1_out), .clr(button_1_out));  // open: en
  Register #(.width(32)) register_10 (
    .D(multiplexer_2_out), .en(wr_last), .Q(register_10_q), .clk(clock_1_out), .clr(button_1_out));
  Register #(.width(32)) register_11 (
    .D(register_9_q), .en(wr_bigger), .Q(register_11_q), .clk(clock_1_out), .clr(button_1_out));
  Comparator #(.width(32)) comparator_1 (.a(register_11_q), .b(register_9_q), .lt(comparator_1_lt));  // open: gt, eq
  Comparator #(.width(32)) comparator_2 (.a(register_9_q), .b(register_10_q), .eq(comparator_2_eq));  // open: gt, lt
endmodule
